# Fritzing sketch circuitttt 1 (saved by Fritzing 0.9.3b)
breadboards: 1

parts:
  Part1 = Arduino Mega 2560 (Rev3)
  2_Channel_Relay1 = 2 Channel Power Relay
  D1 = LTE-302 [package=lte-302]
  D2 = Diode [package=diode-1n4001]
  M1 = DC Motor

nets:
  GND: Part1.GND, 2_Channel_Relay1.GND, D2.C
  N1: Part1.D10_PWM, D1.A
  5V: Part1.5V, 2_Channel_Relay1.VCC
  N2: Part1.D34, 2_Channel_Relay1.IN1
  N3: Part1.D38, 2_Channel_Relay1.IN2
  N4: 2_Channel_Relay1.K1-NC, 2_Channel_Relay1.K1-NO
  N5: 2_Channel_Relay1.K1-COM, M1.pin_1
  N6: 2_Channel_Relay1.K2-NC, 2_Channel_Relay1.K2-NO

custom parts:
  2 Channel Power Relay: A 2 channel power relay. The module operates at 5V.
